# Fritzing sketch iot (saved by Fritzing 1.0.5)
breadboards: 2

parts:
  R1 = Resistor [tolerance=±5% power=0.25W resistance=1000 package=THT]
  Q1 = NPN-Transistor [package="TO92 [THT]"]
  Part1 = InvenSense MPU6050
  Mod1 = Amica NodeMCU DEVKIT 1.0
  U1 = GAS_SENSOR [package=mq-3]
  T1 = LM35 Temperature Sensor [package="TO92 [THT]"]
  LED1 = LED - 5mm [color="Blue (430nm)" current=0.030A package="5 mm [THT]"]
  LED2 = LED - 5mm [color="Red (633nm)" current=0.030A package="5 mm [THT]"]
  RFID1 = RFID Reader
  J1 = Basic Servo
  J2 = Piezo Speaker
  Mod2 = Amica NodeMCU DEVKIT 1.0

nets:
  N1: R1.Pin_0, Mod1.pin5
  N2: R1.Pin_1, Q1.B
  GND: Q1.E, Part1.GND, Mod1.pin2, Mod1.pin_9, Mod1.pin_25, Mod1.pin_29, U1.A1, T1.GND, LED1.cathode
  N3: Q1.C, J2.pin1
  N4: Part1.VCC, Mod1.pin_30, T1.+Vs, LED2.cathode, J2.pin2
  N5: Part1.SCL, Mod1.pin_14
  N6: Part1.SDA, Mod1.pin_13
  N7: Mod1.pin1, Mod1.pin_10, Mod1.pin_26
  N8: Mod1.pin7, LED1.anode
  N9: Mod1.pin8, LED2.anode
  N10: Mod1.pin_15, U1.B1
  N11: Mod1.pin_16, T1.Vout
  GND_2: RFID1.GND, J1.gnd, Mod2.pin2, Mod2.pin_9, Mod2.pin_25, Mod2.pin_29
  N12: RFID1.RES, Mod2.pin_12
  N13: RFID1.CP, Mod2.pin6
  N14: RFID1.+/-, Mod2.pin7
  N15: RFID1.D1, Mod2.pin8
  N16: RFID1.D0, Mod2.pin_11
  +5V: RFID1.+5V, J1.vcc, Mod2.pin1, Mod2.pin_10, Mod2.pin_26
  N17: J1.pulse, Mod2.pin_14

notes:
  MQ-2 Gas Sensor
  RC522 NFC Card Reader
  LM35
  2n2222 transistor
  MPU6050
  passive buzzer
